# Fritzing sketch Actuator Part (saved by Fritzing 0.9.3b)

parts:
  부품3 = Arduino Uno (Rev3)
  U4 = ESP8266 WiFi Module [part_number=ESP8266]
  LED4 = LED - 3mm [color="Red (633nm)" package="3 mm [THT]"]
  S2 = H-Bridge with L298N
  F2 = Fan - Ventilador [package=THT]
  LED5 = LEDs [package=led10mm]  # not connected
  VCC5 = Battery
  VCC6 = Battery  # not connected
  VCC7 = Battery  # not connected
  VCC8 = Battery  # not connected

nets:
  N1: 부품3.D9_PWM, S2.IN2
  N2: 부품3.D10_PWM/SS, S2.ENA
  N3: 부품3.D12/MISO, U4.TXD
  N4: 부품3.D13/SCK, U4.RXD
  N5: 부품3.D6_PWM, LED4.anode
  N6: 부품3.D7, S2.IN1
  N7: S2.12V, VCC5.+
  N8: S2.GND, VCC5.-
  N9: S2.M1-01, F2.5V
  N10: S2.M1-02, F2.GND

custom parts:
  ESP8266 WiFi Module: Generic WiFi Module based on the ESP8266 with onboard PCB antenna and UART communications
  H-Bridge with L298N: h-bridge
  Fan - Ventilador: Ventilador de 2 pines, se encuentra comunmente en computadoras de escritorio
  LEDs: LEDs Standard schematic elements and footprints for 5mm, 3mm, 1206, and 0603 sized LEDs. 5mm - Spark Fun Electronics SKU : COM-00529 (and others)
