# Fritzing sketch Nano_esp8266_DHT11_LED (saved by Fritzing 0.9.3b)

parts:
  U1 = ESP8266 WiFi Module [part_number=ESP8266]
  부품3 = Arduino Nano (Rev3.0) (ICSP)
  LED1 = LEDs [package=led10mm]
  DHT1 = DHT11 Humitidy and Temperature Sensor

nets:
  N1: U1.RXD, 부품3.D12/MISO
  VCC: U1.VCC, 부품3.5V
  GND: U1.GND, 부품3.GND, LED1.C
  N2: U1.TXD, 부품3.D11/MOSI
  N3: 부품3.D3, LED1.A
  N4: 부품3.A0, DHT1.DATA, DHT1.NULL

custom parts:
  ESP8266 WiFi Module: Generic WiFi Module based on the ESP8266 with onboard PCB antenna and UART communications
  DHT11 Humitidy and Temperature Sensor: DHT11 Humidity and Temperature Sensor
