# Fritzing sketch UNO_circuit diagram (saved by Fritzing 0.9.3b)

parts:
  부품1 = Arduino Uno (Rev3)
  DHT1 = DHT11 Humitidy and Temperature Sensor
  U2 = ESP8266 WiFi Module [part_number=ESP8266]
  U3 = Sharp Dust Sensor [part_number=GP2Y1010AU0F]
  MQ-3_Sensor1 = MQ-3 Breakout Board
  LED1 = LED - 3mm [color="Red (633nm)" package="3 mm [THT]"]

nets:
  N1: 부품1.A0, DHT1.NULL
  N2: 부품1.A1, MQ-3_Sensor1.AOUT
  N3: 부품1.A2, U3.Vo
  N4: 부품1.D12/MISO, U2.TXD
  N5: 부품1.D13/SCK, U2.RXD
  N6: 부품1.D3_PWM, LED1.anode
  N7: 부품1.D4, U3.LED

custom parts:
  DHT11 Humitidy and Temperature Sensor: DHT11 Humidity and Temperature Sensor
  ESP8266 WiFi Module: Generic WiFi Module based on the ESP8266 with onboard PCB antenna and UART communications
  Sharp Dust Sensor: Sharp GP2Y1010AU0F Dust Sensor
  MQ-3 Breakout Board: MQ-3 alcohol gas sensor breakout board. Input voltage is 5V. Sensor output is available in analog and digital.
